# Fritzing sketch ventilationbuddy (saved by Fritzing 0.9.3b)
breadboards: 1

parts:
  Part1 = Photon
  KY-1 = Keyes Relay [package=THT]
  RHT1 = Humidity and Temperature Sensor RHT03

nets:
  N1: Part1.A0, RHT1.Data-signal
  N2: Part1.GND, KY-1.ground, RHT1.GND_2
  N3: Part1.D3, KY-1.signal
  3V3: Part1.3V3, KY-1.power, RHT1.Vcc

notes:
  grid-powered via AC-DC converter Meanwell IRM 10-12 (https://www.meanwell-web.com/en-gb/ac-dc-single-output-encapsulated-power-supply-irm--10--12) connected to Photon relay shield

custom parts:
  Keyes Relay: The Keyes 5V relay module is suitable for SCM development, home appliance control. It uses a 5V~12V TIL control signal which can control DC / AC signal.
